// Logisim project alu.circ as structural Verilog: 1 circuit, main circuit main
module main (
  input  [15:0] X,
  input  [15:0] Y,
  input  [2:0] Switch,
  output Equal,
  output [31:0] out_5,
  output [15:0] Result,
  output [15:0] Result_2,
  output Signed_Overflow
);

  wire and_2_out, comparator_1_lt, xnor_1_out, xor_1_out;
  wire [3:0] bit_extender_1_out, bit_extender_2_out;
  wire [15:0] add, addu, \and , mult, \or , sll, slt, srl;
  wire [31:0] bit_extender_3_out, bit_extender_4_out, multiplier_2_out;

  // Probe on X
  // Probe on Y
  // Probe on Switch
  Bit_Extender #(.in_width(16), .out_width(4)) bit_extender_1 (.in(Y), .out(bit_extender_1_out));
  Bit_Extender #(.in_width(16), .out_width(4)) bit_extender_2 (.in(Y), .out(bit_extender_2_out));
  assign \and  = X & Y;  // AND_Gate and_1, 16 bits wide
  assign \or  = X | Y;  // OR_Gate or_1, 16 bits wide
  Adder #(.width(16)) adder_1 (.a(X), .b(Y), .out(addu));  // open: cin, cout
  Comparator #(.width(16)) comparator_1 (.a(X), .b(Y), .eq(Equal), .lt(comparator_1_lt));  // open: gt
  Multiplier #(.width(16)) multiplier_1 (.a(X), .b(Y), .out(mult), .cout(out_5[31:16]));  // open: cin
  assign bit_extender_3_out = {{16{X[15]}}, X};  // Bit_Extender bit_extender_3
  Multiplier #(.width(32)) multiplier_2 (
    .a(bit_extender_3_out), .b(bit_extender_4_out), .out(multiplier_2_out));  // open: cin, cout
  assign bit_extender_4_out = {{16{Y[15]}}, Y};  // Bit_Extender bit_extender_4
  Shifter #(.width(16)) shifter_1 (.in(X), .\dist (bit_extender_1_out), .out(sll));
  Shifter #(.width(16), .shift("lr")) shifter_2 (.in(X), .\dist (bit_extender_2_out), .out(srl));
  Adder #(.width(16)) adder_2 (.a(X), .b(Y), .out(add));  // open: cin, cout
  Multiplexer #(.width(16)) multiplexer_1 (
    .in0({16{1'b0}}), .in1(16'h1), .out(slt), .sel(comparator_1_lt));  // open: en
  xor xor_1 (xor_1_out, add[15], Y[15]);
  xnor xnor_1 (xnor_1_out, Y[15], X[15]);
  // Probe on out_5
  and and_2 (and_2_out, xor_1_out, xnor_1_out);
  Multiplexer #(.select(3)) multiplexer_2 (
    .in0(1'b0), .in1(1'b0), .in2(and_2_out), .in3(1'b0), .in4(1'b0), .in5(1'b0), .in6(1'b0), .in7(1'b0),
    .out(Signed_Overflow), .sel(Switch));  // open: en
  Multiplexer #(.select(3), .width(16)) multiplexer_3 (
    .in0(sll), .in1(srl), .in2(add), .in3(\and ), .in4(\or ), .in5(addu), .in6(slt), .in7(mult),
    .out(out_5[15:0]), .sel(Switch));  // open: en
  // Probe on out_5[15:0]
  // Probe on out_5[31:16]

  assign Result = out_5[15:0];
  assign Result_2 = out_5[31:16];

  // Other names for the same wires on the sheet: overflow = Signed_Overflow; S[2:0] = Switch

  // Notes on the sheet:
  //   INPUTS to your circuit
  //   DON'T CHANGE THE LOCATIONS OF THE INPUTS AND OUTPUTS!
  //   OUTPUTS from your circuit
endmodule
