// Logisim project cpu.circ as structural Verilog: 3 circuits, main circuit main
module main (
  input  [15:0] INSTRUCTION,
  input  CLOCK,
  output [15:0] FETCH_ADDRESS,
  output [15:0] s0_Value,
  output [15:0] s1_Value,
  output [15:0] s2_Value,
  output [15:0] ra_Value,
  output [15:0] sp_Value,
  output [15:0] HI_Value,
  output [15:0] LO_Value
);

  wire ALUSrc, Branch, Branch_Taken, comparator_1_eq, eq, ExtOp, Jump, lui, MemToReg, MemWr, mfhi, mflo, Mul,
       nop, or_1_out, or_2_out, R, RegDst, RegWr, U;
  wire [1:0] rd_2;
  wire [2:0] ALUCtr, bit_extender_1_out, funct, RR2, Write_Address;
  wire [3:0] op;
  wire [5:3] imm_6;
  wire [9:6] imm_10;
  wire [15:0] ALU_A, ALU_B, ALU_Out_R, ALU_Out_R2, bit_extender_2_out, bit_extender_3_out,
       bit_extender_4_out, Jump_address, Mem_Address, Mem_Write_Data, multiplexer_4_out, multiplexer_5_out,
       multiplexer_6_out, multiplexer_8_out, multiplexer_9_out, multiplexer_10_out, next_PC, PC_2, PC_2_q,
       PC_SignExt_imm, RAMout, shifter_1_out, sign_extended_imm, WriteData;

  Comparator #(.width(4)) comparator_1 (.a(4'b1011), .b(op), .eq(comparator_1_eq));  // open: gt, lt
  assign bit_extender_1_out = {{1{1'b0}}, rd_2};  // Bit_Extender bit_extender_1
  assign bit_extender_2_out = {{10{imm_6[5]}}, {imm_6, funct}};  // Bit_Extender bit_extender_2
  assign bit_extender_3_out = {{10{1'b0}}, {imm_6, funct}};  // Bit_Extender bit_extender_3
  Register #(.width(16)) PC (.D(next_PC), .Q(FETCH_ADDRESS), .clk(CLOCK));  // open: en, clr
  Multiplexer #(.width(3), .enable("false")) multiplexer_1 (
    .in0(imm_6), .in1({rd_2, imm_10[9]}), .out(RR2), .sel(or_1_out));
  or or_1 (or_1_out, comparator_1_eq, Branch);
  Multiplexer #(.width(3), .enable("false")) multiplexer_2 (
    .in0({rd_2, imm_10[9]}), .in1(bit_extender_1_out), .out(Write_Address), .sel(RegDst));
  Multiplexer #(.width(16), .enable("false")) multiplexer_3 (
    .in0(bit_extender_2_out), .in1(bit_extender_3_out), .out(sign_extended_imm), .sel(ExtOp));
  Register #(.width(16)) u_PC_2 (.D(FETCH_ADDRESS), .Q(PC_2_q), .clk(CLOCK));  // open: en, clr
  PC_Logic pc_logic_1 (
    .PC(multiplexer_4_out), .imm_6({imm_6, funct}), .imm_10({imm_10, imm_6, funct}), .OpCode(op),
    .Branch(Branch), .Jump(Jump), .U(U), .R_s____SignExt_imm(Mem_Address), .eq(eq), .PC_2(PC_2),
    .Jump_Address(Jump_address), .PC___SignExt_imm(PC_SignExt_imm), .NextPC(next_PC),
    .Branch_Taken(Branch_Taken));
  Multiplexer #(.width(16), .enable("false")) multiplexer_4 (
    .in0(FETCH_ADDRESS), .in1(PC_2_q), .out(multiplexer_4_out), .sel(nop));
  regfile_main main_1 (
    .Read_Register_1(imm_10[8:6]), .Read_Register_2(RR2), .Write_Register(Write_Address),
    .Write_Data(WriteData), .Write_Enable(RegWr), .Clock(CLOCK), .Read_Data_1(ALU_A),
    .Read_Data_2(Mem_Write_Data), .s0_Value(s0_Value), .s1_Value(s1_Value), .s2_Value(s2_Value),
    .ra_Value(ra_Value), .sp_Value(sp_Value));  // open: _0_Value, v0_Value, a0_Value
  assign bit_extender_4_out = {{6{1'b0}}, {imm_10, imm_6, funct}};  // Bit_Extender bit_extender_4
  Register #(.width(16)) HI (.D(ALU_Out_R2), .en(Mul), .Q(HI_Value), .clk(CLOCK));  // open: clr
  Shifter #(.width(16)) shifter_1 (.in(bit_extender_4_out), .\dist (4'b0110), .out(shifter_1_out));
  Multiplexer #(.width(16), .enable("false")) multiplexer_5 (
    .in0(ALU_Out_R), .in1(shifter_1_out), .out(multiplexer_5_out), .sel(lui));
  Register #(.width(16)) LO (.D(multiplexer_5_out), .en(or_2_out), .Q(LO_Value), .clk(CLOCK));  // open: clr
  or or_2 (or_2_out, Mul, lui);
  Control_Unit control_unit_1 (
    .Input({op, rd_2, imm_10, imm_6, funct}), .Jump(Jump), .RegDst(RegDst), .ExtOp(ExtOp), .RegWr(RegWr),
    .ALUSrc(ALUSrc), .ALUCtr(ALUCtr), .MemWr(MemWr), .MemToReg(MemToReg), .Branch(Branch), .Mul(Mul),
    .Iui(lui), .U(U), .mfhi(mfhi), .mflo(mflo), .R(R));
  or or_3 (nop, Branch_Taken, Jump);
  Multiplexer #(.width(16), .enable("false")) multiplexer_6 (
    .in0(INSTRUCTION), .in1({16{1'b0}}), .out(multiplexer_6_out), .sel(nop));
  Register #(.width(16)) register_1 (
    .D(multiplexer_6_out), .Q({op, rd_2, imm_10, imm_6, funct}), .clk(CLOCK));  // open: en, clr
  Multiplexer #(.width(16), .enable("false")) multiplexer_7 (
    .in0(Mem_Write_Data), .in1(sign_extended_imm), .out(ALU_B), .sel(ALUSrc));
  alu_main main_2 (
    .Switch(ALUCtr), .X(ALU_A), .Equal(eq), .Result(ALU_Out_R), .Y(ALU_B), .Result_2(ALU_Out_R2));  // open: Signed_Overflow, out_5
  Multiplexer #(.width(16), .enable("false")) multiplexer_8 (
    .in0(ALU_Out_R), .in1(PC_2), .out(multiplexer_8_out), .sel(Jump));
  Multiplexer #(.width(16), .enable("false")) multiplexer_9 (
    .in0(multiplexer_8_out), .in1(HI_Value), .out(multiplexer_9_out), .sel(mfhi));
  Adder #(.width(16)) adder_1 (.a(ALU_A), .b(sign_extended_imm), .out(Mem_Address));  // open: cin, cout
  Multiplexer #(.width(16), .enable("false")) multiplexer_10 (
    .in0(multiplexer_9_out), .in1(LO_Value), .out(multiplexer_10_out), .sel(mflo));
  mem_main MEM (
    .Address(Mem_Address), .Write_Data(Mem_Write_Data), .Write_En(MemWr), .Clock(CLOCK), .Read_Data(RAMout));
  Multiplexer #(.width(16), .enable("false")) multiplexer_11 (
    .in0(multiplexer_10_out), .in1(RAMout), .out(WriteData), .sel(MemToReg));

  // Other names for the same wires on the sheet: imm_6[2:0] = funct; imm_10[5:0] = {imm_6, funct}; rt[2:0] = imm_6;
  //   RR1[2:0] = imm_10[8:6]; rs[2:0] = imm_10[8:6]; rd_3[2:0] = {rd_2, imm_10[9]}; clk = CLOCK;
  //   fetch_addr[15:0] = FETCH_ADDRESS; HI[15:0] = HI_Value; LO[15:0] = LO_Value;
  //   R_s____SignExt_imm[15:0] = Mem_Address; ra[15:0] = ra_Value; Read_Data_R1[15:0] = ALU_A;
  //   Read_Data_R2[15:0] = Mem_Write_Data; s0[15:0] = s0_Value; s1[15:0] = s1_Value; s2[15:0] = s2_Value;
  //   sp[15:0] = sp_Value

  // Notes on the sheet:
  //   Output
  //   These are outputs/inputs from run.circ
  //   Inputs
  //   These are DEBUG/TEST outputs from your circuit.
endmodule

module Control_Unit (
  input  [15:0] Input,
  output Jump,
  output RegDst,
  output ExtOp,
  output RegWr,
  output ALUSrc,
  output [2:0] ALUCtr,
  output MemWr,
  output MemToReg,
  output Branch,
  output Mul,
  output Iui,
  output U,
  output mfhi,
  output mflo,
  output R
);

  wire and_1_out, and_2_out, and_10_out, load_store_words, or_1_out, xor_1_out;
  wire [2:0] ALUCtr___NonR;

  Multiplexer #(.select(4), .width(3), .disabled(0), .enable("false")) multiplexer_1 (
    .in1(3'b000), .in2(3'b010), .in3(3'b000), .in4(3'b110), .in5(3'b110), .in6(3'b010), .in7(3'b110),
    .in8(3'b011), .in9(3'b100), .in10(3'b010), .in11(3'b010), .in12(3'b000), .in13(3'b000), .in14(3'b000),
    .in15(3'b000), .out(ALUCtr___NonR), .sel(Input[15:12]));  // open: in0
  or or_1 (or_1_out, Branch, Mul, Iui, MemWr);
  not not_1 (RegWr, or_1_out);
  and isR (R, ~Input[15], ~Input[14], ~Input[13], ~Input[12]);  // AND_Gate
  xor xor_1 (xor_1_out, Input[13], Input[12]);
  Multiplexer #(.width(3), .enable("false")) multiplexer_2 (
    .in0(ALUCtr___NonR), .in1(Input[2:0]), .out(ALUCtr), .sel(R));
  and and_1 (and_1_out, ~R, Input[15], ~Input[14]);  // AND_Gate
  or or_2 (ALUSrc, and_1_out, and_2_out);
  and and_2 (and_2_out, ~R, ~Input[15], Input[14], Input[13]);  // AND_Gate
  and and_3 (Jump, ~R, ~Input[15], ~Input[14], Input[13]);  // AND_Gate
  and and_4 (Branch, ~R, ~Input[15], Input[14], ~Input[13]);  // AND_Gate
  and lui (Iui, Input[12], RegDst);
  and and_5 (RegDst, ~R, ~Input[15], ~Input[14], xor_1_out);  // AND_Gate
  and and_6 (load_store_words, ~R, Input[15], ~Input[14], Input[13]);  // AND_Gate
  and and_7 (Mul, R, Input[2], Input[1], Input[0]);
  and and_8 (ExtOp, ~R, Input[15], ~Input[14], ~Input[13]);  // AND_Gate
  and and_9 (mfhi, and_10_out, ~Input[12]);  // AND_Gate
  and and_10 (and_10_out, ~R, Input[15], Input[14], ~Input[13]);  // AND_Gate
  and and_11 (mflo, and_10_out, Input[12]);
  and and_12 (MemToReg, load_store_words, ~Input[12]);  // AND_Gate
  and and_13 (MemWr, load_store_words, Input[12]);

  assign U = RegDst;

  // Other names for the same wires on the sheet: lui = Iui; U_RegDst = RegDst

  // Notes on the sheet:
  //   sll
  //   +
  //   &
  //   |
  //   set less than
endmodule

// PC
module PC_Logic (
  input  [15:0] PC,
  input  [5:0] imm_6,
  input  [9:0] imm_10,
  input  [3:0] OpCode,
  input  Branch,
  input  Jump,
  input  U,
  input  [15:0] R_s____SignExt_imm,
  input  eq,
  output [15:0] PC_2,
  output [15:0] Jump_Address,
  output [15:0] PC___SignExt_imm,
  output [15:0] NextPC,
  output Branch_Taken
);

  wire and_1_out, and_2_out, and_3_out, and_4_out, comparator_1_eq;
  wire [15:0] bit_extender_1_out, bit_extender_2_out, bit_extender_3_out, multiplexer_1_out,
       multiplexer_2_out, shifter_1_out, shifter_2_out;

  assign bit_extender_1_out = {{10{imm_6[5]}}, imm_6};  // Bit_Extender bit_extender_1
  assign bit_extender_2_out = {{6{1'b0}}, imm_10};  // Bit_Extender bit_extender_2
  Comparator #(.width(4), .mode("unsigned")) comparator_1 (
    .a(OpCode), .b(4'b0100), .eq(comparator_1_eq));  // open: gt, lt
  Adder #(.width(16)) adder_1 (.a(16'h2), .b(PC), .out(PC_2));  // open: cin, cout
  assign bit_extender_3_out = {{10{1'b0}}, PC[15:10]};  // Bit_Extender bit_extender_3
  Adder #(.width(16)) adder_2 (.a(PC), .b(bit_extender_1_out), .out(PC___SignExt_imm));  // open: cin, cout
  Shifter #(.width(16)) shifter_1 (.in(bit_extender_3_out), .\dist (4'b1000), .out(shifter_1_out));
  and and_1 (and_1_out, comparator_1_eq, Branch, eq);
  or or_1 (Branch_Taken, and_1_out, and_2_out);
  and and_2 (and_2_out, Branch, ~comparator_1_eq, ~eq);  // AND_Gate
  Shifter #(.width(16)) shifter_2 (.in(shifter_1_out), .\dist (4'b0010), .out(shifter_2_out));
  Multiplexer #(.width(16), .enable("false")) multiplexer_1 (
    .in0(PC_2), .in1(PC___SignExt_imm), .out(multiplexer_1_out), .sel(Branch_Taken));
  Adder #(.width(16)) adder_3 (.a(shifter_2_out), .b(bit_extender_2_out), .out(Jump_Address));  // open: cin, cout
  and and_3 (and_3_out, Jump, U);
  Multiplexer #(.width(16), .enable("false")) multiplexer_2 (
    .in0(multiplexer_1_out), .in1(Jump_Address), .out(multiplexer_2_out), .sel(and_3_out));
  Multiplexer #(.width(16), .enable("false")) multiplexer_3 (
    .in0(multiplexer_2_out), .in1(R_s____SignExt_imm), .out(NextPC), .sel(and_4_out));
  and and_4 (and_4_out, Jump, ~U);  // AND_Gate

  // Other names for the same wires on the sheet: next_PC[15:0] = NextPC; PC_SignExt_imm[15:0] = PC___SignExt_imm
endmodule
