// Logisim project mem.circ as structural Verilog: 1 circuit, main circuit main
module main (
  input  [15:0] Address,
  input  [15:0] Write_Data,
  input  Write_En,
  input  Clock,
  output [15:0] Read_Data
);

  RAM #(.addrWidth(14), .dataWidth(16), .bus("separate")) ram_1 (
    .addr(Address[14:1]), .din(Write_Data), .data(Read_Data), .str(Write_En), .sel(1'b1), .clk(Clock),
    .ld(1'b1), .clr(1'b0));
endmodule
