// Logisim project regfile.circ as structural Verilog: 1 circuit, main circuit main
module main (
  input  [2:0] Read_Register_1,
  input  [2:0] Read_Register_2,
  input  [2:0] Write_Register,
  input  [15:0] Write_Data,
  input  Write_Enable,
  input  Clock,
  output [15:0] _0_Value,
  output [15:0] a0_Value,
  output [15:0] v0_Value,
  output [15:0] s0_Value,
  output [15:0] s1_Value,
  output [15:0] s2_Value,
  output [15:0] ra_Value,
  output [15:0] sp_Value,
  output [15:0] Read_Data_1,
  output [15:0] Read_Data_2
);

  wire and_1_out, and_2_out, and_3_out, and_4_out, and_5_out, and_6_out, and_7_out, and_8_out, write_reg0,
       write_reg1, write_reg2, write_reg3, write_reg4, write_reg5, write_reg6, write_reg7;

  and and_1 (and_1_out, write_reg0, 1'b0);
  and and_2 (and_2_out, write_reg1, Write_Enable);
  and and_3 (and_3_out, write_reg2, Write_Enable);
  and and_4 (and_4_out, write_reg3, Write_Enable);
  and and_5 (and_5_out, write_reg4, Write_Enable);
  and and_6 (and_6_out, write_reg5, Write_Enable);
  and and_7 (and_7_out, write_reg6, Write_Enable);
  and and_8 (and_8_out, write_reg7, Write_Enable);
  Register #(.width(16)) register_1 (.D(Write_Data), .en(and_1_out), .Q(_0_Value), .clk(Clock));  // open: clr
  Register #(.width(16)) register_2 (.D(Write_Data), .en(and_2_out), .Q(ra_Value), .clk(Clock));  // open: clr
  Register #(.width(16)) register_3 (.D(Write_Data), .en(and_3_out), .Q(s0_Value), .clk(Clock));  // open: clr
  Register #(.width(16)) register_4 (.D(Write_Data), .en(and_4_out), .Q(s1_Value), .clk(Clock));  // open: clr
  Register #(.width(16)) register_5 (.D(Write_Data), .en(and_5_out), .Q(s2_Value), .clk(Clock));  // open: clr
  Register #(.width(16)) register_6 (.D(Write_Data), .en(and_6_out), .Q(a0_Value), .clk(Clock));  // open: clr
  Register #(.width(16)) register_7 (.D(Write_Data), .en(and_7_out), .Q(v0_Value), .clk(Clock));  // open: clr
  Register #(.width(16)) register_8 (.D(Write_Data), .en(and_8_out), .Q(sp_Value), .clk(Clock));  // open: clr
  Decoder #(.select(3)) decoder_1 (
    .out0(write_reg0), .out1(write_reg1), .out2(write_reg2), .out3(write_reg3), .out4(write_reg4),
    .out5(write_reg5), .out6(write_reg6), .out7(write_reg7), .sel(Write_Register));  // open: en
  Multiplexer #(.select(3), .width(16)) multiplexer_1 (
    .in0(_0_Value), .in1(ra_Value), .in2(s0_Value), .in3(s1_Value), .in4(s2_Value), .in5(a0_Value),
    .in6(v0_Value), .in7(sp_Value), .out(Read_Data_1), .sel(Read_Register_1));  // open: en
  Multiplexer #(.select(3), .width(16)) multiplexer_2 (
    .in0(_0_Value), .in1(ra_Value), .in2(s0_Value), .in3(s1_Value), .in4(s2_Value), .in5(a0_Value),
    .in6(v0_Value), .in7(sp_Value), .out(Read_Data_2), .sel(Read_Register_2));  // open: en

  // Other names for the same wires on the sheet: _0[15:0] = _0_Value; a0[15:0] = a0_Value; clk = Clock;
  //   ra[15:0] = ra_Value; read_data1[15:0] = Read_Data_1; read_data2[15:0] = Read_Data_2;
  //   read_reg1[2:0] = Read_Register_1; read_reg2[2:0] = Read_Register_2; s0[15:0] = s0_Value; s1[15:0] = s1_Value;
  //   s2[15:0] = s2_Value; sp[15:0] = sp_Value; v0[15:0] = v0_Value; write_en = Write_Enable;
  //   write_reg[2:0] = Write_Register

  // Notes on the sheet:
  //   INPUTS to your circuit
  //   DON'T CHANGE THE LOCATIONS OF THE INPUTS AND OUTPUTS!
  //   These are DEBUG/TEST outputs from your circuit.
  //   OUTPUTS from your circuit
endmodule
